# Fritzing sketch blinkAndPush (saved by Fritzing 0.9.3b)
circuit board: 6.88566cm x 5.36311cm
breadboards: 1

parts:
  LED = LED - 5mm [color="Red (633nm)" package="5 mm [THT]"]
  Arduino1 = Arduino Uno (Rev3)
  R1 = Resistor [tolerance=±5% resistance=220 package=THT]
  S1 = Pushbutton [package="[SMD]"]
  R2 = Trimmer Potentiometer [maximum_resistance=10kΩ package=THT]  # not connected

nets:
  N1: LED.cathode, Arduino1.GND, R1.Pin_0
  N2: LED.anode, Arduino1.D13/SCK
  N3: Arduino1.D3_PWM, R1.Pin_1, S1.Pin_1, S1.Pin_2
  N4: Arduino1.5V, S1.Pin_3, S1.Pin_4

notes:
  BLINK

// code stored in the sketch: Blink.ino
/*
  Blink


  Turns an LED on for one second, then off for one second, repeatedly.


  Most Arduinos have an on-board LED you can control. On the UNO, MEGA and ZERO
  it is attached to digital pin 13, on MKR1000 on pin 6. LED_BUILTIN is set to
  the correct LED pin independent of which board is used.
  If you want to know what pin the on-board LED is connected to on your Arduino
  model, check the Technical Specs of your board at:
  https://www.arduino.cc/en/Main/Products


  modified 8 May 2014
  by Scott Fitzgerald
  modified 2 Sep 2016
  by Arturo Guadalupi
  modified 8 Sep 2016
  by Colby Newman


  This example code is in the public domain.


  https://www.arduino.cc/en/Tutorial/BuiltInExamples/Blink
*/


// the setup function runs once when you press reset or power the board
void setup() {
  // initialize digital pin LED_BUILTIN as an output.
  pinMode(LED_BUILTIN, OUTPUT);
  pinMode(2, INPUT);
}


// the loop function runs over and over again forever
void loop() {
  if (digitalRead(2) == HIGH) {
    blink(LED_BUILTIN);
  }
  delay(5000);
}


void blink(int pin) {
  digitalWrite(pin, HIGH);  // turn the LED on (HIGH is the voltage level)
  delay(1000);              // wait for a second
  digitalWrite(pin, LOW);   // turn the LED off by making the voltage LOW
  delay(1000);              // wait for a second
}
